// Logisim project 8-bit One's Complement.circ as structural Verilog: 1 circuit, main circuit main
module main (
  input  in_1,
  input  in_2,
  input  in_3,
  input  in_4,
  input  in_5,
  input  in_6,
  input  in_7,
  input  in_8,
  input  in_9,
  output out_10,
  output out_11,
  output out_12,
  output out_13,
  output out_14,
  output out_15,
  output out_16,
  output out_17
);

  xor xor_1 (out_10, in_1, in_9);
  xor xor_2 (out_11, in_2, in_9);
  xor xor_3 (out_12, in_3, in_9);
  xor xor_4 (out_13, in_4, in_9);
  xor xor_5 (out_14, in_5, in_9);
  xor xor_6 (out_15, in_6, in_9);
  xor xor_7 (out_16, in_7, in_9);
  xor xor_8 (out_17, in_8, in_9);
endmodule
